# Fritzing sketch Clock_With_Alarm (saved by Fritzing 0.9.3b)
breadboards: 1

parts:
  U1 = LCD-16X2 [package=lcd-16x2_noholes]
  U2 = POT [package=pot_mammoth]
  ZS-042_RTC1 = ZS-042 RTC Module
  Part1 = Arduino Uno (Rev3)
  R1 = Resistor [tolerance=±5% resistance=220 package="0402 [SMD]"]
  S1 = Momentary Switch [package=ksa_sealed_tac_switch]
  S2 = Momentary Switch [package=ksa_sealed_tac_switch]
  S3 = Momentary Switch [package=ksa_sealed_tac_switch]

nets:
  VSS: U1.VSS, U1.R_W, U1.K, U2.E, ZS-042_RTC1.GND, S1.1, S2.1, S3.1
  VDD: U1.VDD, U2.S, ZS-042_RTC1.VCC, R1.Pin_0
  N1: U1.VO, U2.A
  N2: U1.RS, Part1.D2
  N3: U1.E, Part1.D3_PWM
  N4: U1.DB4, Part1.D4
  N5: U1.DB5, Part1.D5_PWM
  N6: U1.DB6, Part1.D6_PWM
  N7: U1.DB7, Part1.D7
  N8: U1.A, R1.Pin_1
  N9: ZS-042_RTC1.SDA, Part1.A4/SDA
  N10: ZS-042_RTC1.SCL, Part1.A5/SCL
  N11: Part1.A1, S2.4
  N12: Part1.A2, S3.4
  N13: Part1.A3, S1.4
